// Logisim project expr.circ as structural Verilog: 1 circuit, main circuit main
module main (
  input  A,
  input  B,
  input  C,
  output Z1,
  output X,
  output Z4,
  output Z3,
  output Z2
);

  not not_1 (Z1, A);
  not not_2 (Z2, C);
  or or_1 (Z3, B, Z2);
  not not_3 (Z4, Z3);
  or or_2 (X, Z1, Z4);
endmodule
