// Logisim project equivalenza2_confronto.circ as structural Verilog: 1 circuit, main circuit main
module main (
  input  A,
  input  B,
  input  C,
  output nA,
  output A_v_B,
  output A_NOR_B,
  output nB,
  output A_NOR_B_____C_v_nB,
  output C_v_nB,
  output nC,
  output out_11,
  output nA_2,
  output nA___nB,
  output nB_2
);

  wire nand_8_out, nand_11_out;

  nand nand_1 (nA, A, A);
  nand nand_2 (nB, B, B);
  nand nand_3 (nC, C, C);
  nand nand_4 (nA_2, A, A);
  nand nand_5 (nB_2, B, B);
  nand nand_6 (A_v_B, nA, nB);
  nand nand_7 (C_v_nB, B, nC);
  nand nand_8 (nand_8_out, nA_2, nB_2);
  nand nand_9 (A_NOR_B, A_v_B, A_v_B);
  nand nand_10 (nA___nB, nand_8_out, nand_8_out);
  nand nand_11 (nand_11_out, A_NOR_B, C_v_nB);
  nand nand_12 (A_NOR_B_____C_v_nB, nand_11_out, nand_11_out);
  xnor xnor_1 (out_11, A_NOR_B_____C_v_nB, nA___nB);
endmodule
