// Logisim project espressione_formula_originale.circ as structural Verilog: 1 circuit, main circuit main
module main (
  input  A,
  input  B,
  input  C,
  input  D,
  output Z_1,
  output Z_4,
  output Z_2,
  output X,
  output Z_3
);

  wire and_2_out;

  or or_1 (Z_1, A, ~B);  // OR_Gate
  or or_2 (Z_2, B, C);
  and and_1 (Z_3, ~B, D);  // AND_Gate
  and and_2 (and_2_out, A, Z_1);
  and and_3 (Z_4, and_2_out, Z_2);
  or or_3 (X, Z_4, Z_3);
endmodule
