// Logisim project halfadder.circ as structural Verilog: 1 circuit, main circuit main
module main (
  input  A,
  input  B,
  output R,
  output S
);

  xor xor_1 (S, A, B);
  and and_1 (R, A, B);
endmodule
