// Logisim project fullader_SOP.circ as structural Verilog: 1 circuit, main circuit main
module main (
  input  R_IN,
  input  A,
  input  B,
  output S,
  output R_OUT
);

  wire and_1_out, and_2_out, and_3_out, and_4_out, and_5_out, and_6_out, and_7_out;

  and and_1 (and_1_out, ~R_IN, ~A, B);  // AND_Gate
  and and_2 (and_2_out, ~R_IN, A, ~A);  // AND_Gate
  and and_3 (and_3_out, R_IN, ~A, ~B);  // AND_Gate
  and and_4 (and_4_out, R_IN, A, B);
  and and_5 (and_5_out, R_IN, A, ~B);  // AND_Gate
  and and_6 (and_6_out, R_IN, ~A, B);  // AND_Gate
  and and_7 (and_7_out, ~R_IN, A, B);  // AND_Gate
  or or_1 (S, and_1_out, and_2_out, and_3_out, and_4_out);
  or or_2 (R_OUT, and_4_out, and_5_out, and_6_out, and_7_out);
endmodule
