// Logisim project miniALU.circ as structural Verilog: 1 circuit, main circuit main
module main (
  input  [3:0] A,
  input  X,
  input  in_3,
  input  [3:0] B,
  output [3:0] out_5,
  output overflow,
  output [3:0] additional
);

  wire main_1_overflow, or_1_out;
  wire [3:0] main_1_risultato, undriven;

  sommaDifferenzaOverflow_main main_1 (
    .B(B), .A(B), .in_3(in_3), .risultato(main_1_risultato), .overflow(main_1_overflow));  // open: out_5
  // _4_bit_Multiplier 4_bit_multiplier_1: pin names not known; wires that end beside it: additional[0], additional[1], additional[2], additional[3]
  Multiplexer #(.width(4), .enable("false")) multiplexer_1 (
    .in0(main_1_risultato), .in1(undriven), .out(out_5), .sel(X));
  Multiplexer #(.enable("false")) multiplexer_2 (.in0(main_1_overflow), .in1(or_1_out), .out(overflow), .sel(X));
  or or_1 (or_1_out, additional[0], additional[1], additional[2], additional[3]);
endmodule
