// Logisim project sommaDifferenzaOverflow.circ as structural Verilog: 1 circuit, main circuit main
module main (
  input  [3:0] B,
  input  [3:0] A,
  input  in_3,
  output [3:0] risultato,
  output out_5,
  output overflow
);

  wire xor_5_out, xor_6_out;
  wire [3:0] xor_2_out;

  Adder #(.width(4)) adder_1 (.a(xor_2_out), .b(A), .out(risultato), .cin(in_3), .cout(out_5));
  xor xor_1 (xor_2_out[1], in_3, B[1]);
  xor xor_2 (xor_2_out[0], in_3, B[0]);
  xor xor_3 (xor_2_out[2], in_3, B[2]);
  xor xor_4 (xor_2_out[3], in_3, B[3]);
  xor xor_5 (xor_5_out, xor_2_out[3], risultato[3]);
  xor xor_6 (xor_6_out, risultato[3], A[3]);
  and and_1 (overflow, xor_5_out, xor_6_out);

  // Notes on the sheet:
  //   A e B sono numeri in complemento a 2
  //   segno secondo operando
  //   segno risultato
  //   segno primo operando
endmodule
