// Logisim project bistabile_SOP_X1.circ as structural Verilog: 1 circuit, main circuit Latch SR
module Latch_SR (
  input  Reset,
  input  Set,
  output Q
);

  wire and_1_out;

  or or_1 (Q, Set, and_1_out);
  and and_1 (and_1_out, Q, ~Reset);  // AND_Gate
endmodule
