// Logisim project bistabile_SOP_oscillazione.circ as structural Verilog: 1 circuit, main circuit Latch SC
module Latch_SC (
  output out_1
);

  wire and_1_out, and_2_out, and_3_out, Reset_out, Set_out;

  Button Reset (.out(Reset_out));
  Button Set (.out(Set_out));
  and and_1 (and_1_out, ~Reset_out, ~Set_out);  // AND_Gate
  and and_2 (and_2_out, ~Reset_out, Set_out);  // AND_Gate
  and and_3 (and_3_out, out_1, and_1_out);
  or or_1 (out_1, and_3_out, and_2_out);
endmodule
