// Logisim project bistabile_SOP_oscillazione_risolta.circ as structural Verilog: 1 circuit, main circuit Latch SR
module Latch_SR (
  output out_1
);

  wire and_1_out, and_2_out, and_3_out, and_4_out, Reset_out, Set_out;

  Button Reset (.out(Reset_out));
  Button Set (.out(Set_out));
  and and_1 (and_1_out, ~Reset_out, ~Set_out);  // AND_Gate
  and and_2 (and_2_out, ~Reset_out, Set_out);  // AND_Gate
  and and_3 (and_3_out, out_1, and_1_out);
  and and_4 (and_4_out, 1'b1, and_2_out);
  or or_1 (out_1, and_3_out, and_4_out);
endmodule
