// Logisim project bistabile_v2-tunnel.circ as structural Verilog: 1 circuit, main circuit Latch SC
module Latch_SC (
  output Q,
  output nQ
);

  wire Reset_out, Set_out;

  Button Reset (.out(Reset_out));
  Button Set (.out(Set_out));
  nor nor_1 (Q, Reset_out, nQ);
  nor nor_2 (nQ, Q, Set_out);
endmodule
