// Logisim project bistabile_sincrono.circ as structural Verilog: 2 circuits, main circuit Latch SR sync
module Latch_SR (
  input  Reset,
  input  Set,
  output Q,
  output nQ
);

  nor nor_1 (Q, Reset, nQ);
  nor nor_2 (nQ, Q, Set);
endmodule

module Latch_SR_sync (
  output Q,
  output nQ
);

  wire and_1_out, and_2_out, Clock_out, Reset_out, Set_out;

  Button Reset (.out(Reset_out));
  Clock Clock (.out(Clock_out));
  Button Set (.out(Set_out));
  and and_1 (and_1_out, Reset_out, Clock_out);
  and and_2 (and_2_out, Clock_out, Set_out);
  Latch_SR latch_sr_1 (.Reset(and_1_out), .Set(and_2_out), .Q(Q), .nQ(nQ));
endmodule
