// Logisim project memoria_4D.circ as structural Verilog: 4 circuits, main circuit Banco memoria 4 bit
module Latch_SR (
  input  Reset,
  input  Set,
  output Q,
  output nQ
);

  nor nor_1 (Q, Reset, nQ);
  nor nor_2 (nQ, Q, Set);
endmodule

module Latch_SR_sync (
  input  Reset,
  input  Clock,
  input  Set,
  output Q,
  output nQ
);

  wire and_1_out, and_2_out;

  and and_1 (and_1_out, Reset, Clock);
  and and_2 (and_2_out, Clock, Set);
  Latch_SR latch_sr_1 (.Reset(and_1_out), .Set(and_2_out), .Q(Q), .nQ(nQ));
endmodule

module Latch_D_sync (
  input  D,
  input  Clock,
  output Q,
  output nQ
);

  wire not_1_out;

  not not_1 (not_1_out, D);
  Latch_SR_sync latch_sr_sync_1 (.Reset(not_1_out), .Clock(Clock), .Set(D), .Q(Q), .nQ(nQ));
endmodule

module Banco_memoria_4_bit (
  input  [3:0] _4_bit_da_memorizzare,
  input  Write,
  output [3:0] out_3
);

  wire and_1_out, Clock_out;

  Clock Clock (.out(Clock_out));
  and and_1 (and_1_out, Clock_out, Write);
  Latch_D_sync latch_d_sync_1 (.D(_4_bit_da_memorizzare[0]), .Clock(and_1_out), .Q(out_3[0]));  // open: nQ
  Latch_D_sync latch_d_sync_2 (.D(_4_bit_da_memorizzare[1]), .Clock(and_1_out), .Q(out_3[1]));  // open: nQ
  Latch_D_sync latch_d_sync_3 (.D(_4_bit_da_memorizzare[2]), .Clock(and_1_out), .Q(out_3[2]));  // open: nQ
  Latch_D_sync latch_d_sync_4 (.D(_4_bit_da_memorizzare[3]), .Clock(and_1_out), .Q(out_3[3]));  // open: nQ
endmodule
