// Logisim project memoria_4D_azzeramento.circ as structural Verilog: 5 circuits, main circuit 4-bit Word Write Reset sync
module Latch_SC (
  input  Clear,
  input  Set,
  output Q,
  output nQ
);

  nor nor_1 (Q, Clear, nQ);
  nor nor_2 (nQ, Q, Set);
endmodule

module Latch_SC_sync (
  input  Clear,
  input  Clock,
  input  Set,
  output Q,
  output nQ
);

  wire and_1_out, and_2_out;

  and and_1 (and_1_out, Clear, Clock);
  and and_2 (and_2_out, Clock, Set);
  Latch_SC latch_sc_1 (.Clear(and_1_out), .Set(and_2_out), .Q(Q), .nQ(nQ));
endmodule

module Latch_D_sync (
  input  D,
  input  Clock,
  output Q,
  output out_4
);

  wire not_1_out;

  not not_1 (not_1_out, D);
  Latch_SC_sync latch_sc_sync_1 (.Clear(not_1_out), .Clock(Clock), .Set(D), .Q(Q), .nQ(out_4));
endmodule

module Es_4 (
  input  [3:0] in_1,
  input  Clock,
  input  Write,
  output [3:0] out_4
);

  wire and_1_out;

  and and_1 (and_1_out, Clock, Write);
  Latch_D_sync latch_d_sync_1 (.D(in_1[0]), .Clock(and_1_out), .Q(out_4[0]));  // open: out_4
  Latch_D_sync latch_d_sync_2 (.D(in_1[1]), .Clock(and_1_out), .Q(out_4[1]));  // open: out_4
  Latch_D_sync latch_d_sync_3 (.D(in_1[2]), .Clock(and_1_out), .Q(out_4[2]));  // open: out_4
  Latch_D_sync latch_d_sync_4 (.D(in_1[3]), .Clock(and_1_out), .Q(out_4[3]));  // open: out_4
endmodule

module _4_bit_Word_Write_Reset_sync (
  input  [3:0] in_1,
  input  Reset,
  input  Write,
  output [3:0] out_4
);

  wire Clock_out, or_1_out;
  wire [3:0] and_1_out;
  wire [3:3] not_1_out;

  Clock Clock (.out(Clock_out));
  not not_1 (not_1_out[3], Reset);
  or or_1 (or_1_out, Reset, Write);
  assign and_1_out = in_1 & {4{not_1_out[3]}};  // AND_Gate and_1, 4 bits wide
  Es_4 es_4_1 (.in_1(and_1_out), .Clock(Clock_out), .Write(or_1_out), .out_4(out_4));
endmodule
