// Logisim project memoria_indirizzamento.circ as structural Verilog: 2 circuits, main circuit main
module _4_bit_register (
  input  clock,
  input  [3:0] word,
  input  Reset,
  input  Enable,
  output out_5,
  output out_6,
  output out_7,
  output out_8
);

  D_Flip_Flop d_ff_1 (.clk(clock), .D(word[0]), .Q(out_5), .en(Enable), .reset(Reset));  // open: Qn, preset
  D_Flip_Flop d_ff_2 (.clk(clock), .D(word[1]), .Q(out_6), .en(Enable), .reset(Reset));  // open: Qn, preset
  D_Flip_Flop d_ff_3 (.clk(clock), .D(word[2]), .Q(out_7), .en(Enable), .reset(Reset));  // open: Qn, preset
  D_Flip_Flop d_ff_4 (.clk(clock), .D(word[3]), .Q(out_8), .en(Enable), .reset(Reset));  // open: Qn, preset

  // Other names for the same wires on the sheet: E = Enable; R = Reset
endmodule

module main (
  input  Reset,
  input  Write,
  input  [3:0] Word,
  input  [1:0] Address,
  output [15:0] out_5
);

  wire and_1_out, and_2_out, and_3_out, and_4_out, clock_1_out, decoder_1_out0, decoder_1_out1,
       decoder_1_out2, decoder_1_out3;

  Decoder #(.select(2), .enable("false")) decoder_1 (
    .out0(decoder_1_out0), .out1(decoder_1_out1), .out2(decoder_1_out2), .out3(decoder_1_out3), .sel(Address));
  Clock clock_1 (.out(clock_1_out));
  and and_1 (and_1_out, clock_1_out, decoder_1_out0);
  and and_2 (and_2_out, clock_1_out, decoder_1_out1);
  and and_3 (and_3_out, clock_1_out, decoder_1_out2);
  and and_4 (and_4_out, clock_1_out, decoder_1_out3);
  _4_bit_register u_4_bit_register_1 (
    .clock(and_1_out), .word(Word), .Reset(Reset), .out_5(out_5[0]), .out_6(out_5[1]), .out_7(out_5[2]),
    .out_8(out_5[3]), .Enable(Write));
  _4_bit_register u_4_bit_register_2 (
    .clock(and_2_out), .word(Word), .Reset(Reset), .out_5(out_5[4]), .out_6(out_5[5]), .out_7(out_5[6]),
    .out_8(out_5[7]), .Enable(Write));
  _4_bit_register u_4_bit_register_3 (
    .clock(and_3_out), .word(Word), .Reset(Reset), .out_5(out_5[8]), .out_6(out_5[9]), .out_7(out_5[10]),
    .out_8(out_5[11]), .Enable(Write));
  _4_bit_register u_4_bit_register_4 (
    .clock(and_4_out), .word(Word), .Reset(Reset), .out_5(out_5[12]), .out_6(out_5[13]), .out_7(out_5[14]),
    .out_8(out_5[15]), .Enable(Write));
endmodule
