// Logisim project addmod8.circ as structural Verilog: 2 circuits, main circuit main
module main (
);

  wire clock_1_out;
  wire [2:0] add_mod_8_1_q012_star, d_ff_1_q;

  Clock clock_1 (.out(clock_1_out));
  D_Flip_Flop d_ff_1 (.clk(clock_1_out), .D(add_mod_8_1_q012_star[0]), .Q(d_ff_1_q[0]));  // open: Qn, preset, en, reset
  D_Flip_Flop d_ff_2 (.clk(clock_1_out), .D(add_mod_8_1_q012_star[1]), .Q(d_ff_1_q[1]));  // open: Qn, preset, en, reset
  D_Flip_Flop d_ff_3 (.clk(clock_1_out), .D(add_mod_8_1_q012_star[2]), .Q(d_ff_1_q[2]));  // open: Qn, preset, en, reset
  add__mod_8 add_mod_8_1 (.Q012(d_ff_1_q), .Q012_star(add_mod_8_1_q012_star));
  Hex_Digit_Display hex_digit_display_1 (.value({1'b0, d_ff_1_q}));  // open: dp
endmodule

module add__mod_8 (
  input  [2:0] Q012,
  output [2:0] Q012_star
);

  wire and_1_out;

  and and_1 (and_1_out, Q012[0], Q012[1]);
  not not_1 (Q012_star[0], Q012[0]);
  xor xor_1 (Q012_star[1], Q012[0], Q012[1]);
  xor xor_2 (Q012_star[2], and_1_out, Q012[2]);
endmodule
