// Logisim project gray.circ as structural Verilog: 2 circuits, main circuit main
module main (
);

  wire clock_1_out;
  wire [2:0] d_ff_1_q;
  wire [3:0] grayseq_1_q012_star;

  Clock clock_1 (.out(clock_1_out));
  D_Flip_Flop d_ff_1 (.clk(clock_1_out), .D(grayseq_1_q012_star[0]), .Q(d_ff_1_q[0]));  // open: Qn, preset, en, reset
  D_Flip_Flop d_ff_2 (.clk(clock_1_out), .D(grayseq_1_q012_star[1]), .Q(d_ff_1_q[1]));  // open: Qn, preset, en, reset
  D_Flip_Flop d_ff_3 (.clk(clock_1_out), .D(grayseq_1_q012_star[2]), .Q(d_ff_1_q[2]));  // open: Qn, preset, en, reset
  grayseq grayseq_1 (.Q012({1'b0, d_ff_1_q}), .Q012_star(grayseq_1_q012_star));
endmodule

module grayseq (
  input  [3:0] Q012,
  output [3:0] Q012_star
);

  wire and_1_out, and_2_out, and_3_out, or_1_out;

  xnor xnor_1 (Q012_star[0], Q012[1], Q012[2]);
  and and_1 (and_1_out, Q012[1], ~Q012[0]);  // AND_Gate
  or or_1 (or_1_out, Q012[1], Q012[0]);
  and and_2 (and_2_out, or_1_out, ~Q012[2]);  // AND_Gate
  and and_3 (and_3_out, or_1_out, Q012[2]);
  or or_2 (Q012_star[1], and_1_out, and_2_out);
  or or_3 (Q012_star[2], and_3_out, and_1_out);

  assign Q012_star[3] = Q012[3];
endmodule
