// Logisim project cnc.circ as structural Verilog: 2 circuits, main circuit main
module main (
  input  Reset,
  input  plus_1
);

  wire and_1_out, and_2_out, clock_1_out, xor_1_out;
  wire [3:0] adder_1_out, multiplexer_1_out, multiplexer_2_out, Q;

  Clock clock_1 (.out(clock_1_out));
  xor xor_1 (xor_1_out, Reset, plus_1);
  and and_1 (and_1_out, xor_1_out, clock_1_out);
  Hex_Digit_Display hex_digit_display_1 (.value(Q));  // open: dp
  D_Flip_Flop d_ff_1 (.clk(and_1_out), .D(multiplexer_2_out[0]), .Q(Q[0]));  // open: Qn, preset, en, reset
  D_Flip_Flop d_ff_2 (.clk(and_1_out), .D(multiplexer_2_out[1]), .Q(Q[1]));  // open: Qn, preset, en, reset
  D_Flip_Flop d_ff_3 (.clk(and_1_out), .D(multiplexer_2_out[2]), .Q(Q[2]));  // open: Qn, preset, en, reset
  D_Flip_Flop d_ff_4 (.clk(and_1_out), .D(multiplexer_2_out[3]), .Q(Q[3]));  // open: Qn, preset, en, reset
  and and_2 (and_2_out, Q[0], Q[1], Q[2], Q[3]);
  Adder #(.width(4)) adder_1 (.a(Q), .b(4'b0001), .out(adder_1_out));  // open: cin, cout
  Multiplexer #(.width(4), .enable("false")) multiplexer_1 (
    .in0(adder_1_out), .in1(Q), .out(multiplexer_1_out), .sel(and_2_out));
  Multiplexer #(.width(4), .enable("false")) multiplexer_2 (
    .in0(multiplexer_1_out), .in1(4'b0000), .out(multiplexer_2_out), .sel(Reset));

  // Other names for the same wires on the sheet: c = Reset
endmodule

module add (
  input  [3:0] in_1,
  output [3:0] out_2
);

  Adder #(.width(4)) adder_1 (.a(in_1), .b(4'b0001), .out(out_2));  // open: cin, cout
endmodule
