// Logisim project riconoscitore.circ as structural Verilog: 3 circuits, main circuit main
module main (
  input  x,
  output \output 
);

  wire clock_1_out, d_ff_1_q, d_ff_2_q, d_ff_3_q, next_1_b_prime_0, next_1_b_prime_1, next_1_b_prime_2;

  Clock clock_1 (.out(clock_1_out));
  next next_1 (
    .x(x), .b0(d_ff_1_q), .b1(d_ff_2_q), .b2(d_ff_3_q), .b_prime_0(next_1_b_prime_0),
    .b_prime_1(next_1_b_prime_1), .b_prime_2(next_1_b_prime_2));
  D_Flip_Flop d_ff_1 (.clk(clock_1_out), .D(next_1_b_prime_0), .Q(d_ff_1_q));  // open: Qn, preset, en, reset
  D_Flip_Flop d_ff_2 (.clk(clock_1_out), .D(next_1_b_prime_1), .Q(d_ff_2_q));  // open: Qn, preset, en, reset
  D_Flip_Flop d_ff_3 (.clk(clock_1_out), .D(next_1_b_prime_2), .Q(d_ff_3_q));  // open: Qn, preset, en, reset
  \output  output_1 (.\output (\output ), .b0(d_ff_1_q), .b1(d_ff_2_q), .b2(d_ff_3_q));
endmodule

module next (
  input  x,
  input  b0,
  input  b1,
  input  b2,
  output b_prime_0,
  output b_prime_1,
  output b_prime_2
);


  assign b_prime_0 = x;
  assign b_prime_1 = b0;
  assign b_prime_2 = b1;
  // also tied to GND on the sheet: b2
endmodule

module \output  (
  input  b0,
  input  b1,
  input  b2,
  output \output 
);

  wire and_1_out, and_2_out;

  and and_1 (and_1_out, ~b0, b1, ~b2);  // AND_Gate
  and and_2 (and_2_out, b0, ~b1, b2);  // AND_Gate
  or or_1 (\output , and_1_out, and_2_out);
endmodule
