// Logisim project controller_navicella.circ as structural Verilog: 12 circuits, main circuit main
module player (
  input  L_button,
  input  R_button,
  input  Clock,
  output [7:0] position
);

  wire and_1_out, xor_1_out;

  and and_1 (and_1_out, R_button, ~L_button);  // AND_Gate
  xor xor_1 (xor_1_out, R_button, L_button);
  PlayerPos playerpos_1 (.out_4(position), .LR(and_1_out), .MOVE(xor_1_out), .CLOCK(Clock));
endmodule

module s0 (
  input  [7:0] in_1,
  input  I,
  output out_3
);

  wire and_1_out, and_2_out, and_3_out;

  and and_1 (and_1_out, in_1[7], ~in_1[6], ~in_1[5], ~in_1[4], ~in_1[3], ~in_1[2], ~in_1[1], ~in_1[0], ~I);  // AND_Gate
  and and_2 (and_2_out, ~in_1[7], in_1[6], ~in_1[5], ~in_1[4], ~in_1[3], ~in_1[2], ~in_1[1], ~in_1[0], ~I);  // AND_Gate
  and and_3 (and_3_out, ~in_1[7], ~in_1[6], ~in_1[5], ~in_1[4], ~in_1[3], ~in_1[2], ~in_1[1], ~in_1[0]);  // AND_Gate
  or or_1 (out_3, and_1_out, and_3_out, and_2_out);
endmodule

module s1 (
  input  [7:0] in_1,
  input  I,
  output out_3
);

  wire and_1_out, and_2_out;

  and and_1 (and_1_out, in_1[7], ~in_1[6], ~in_1[5], ~in_1[4], ~in_1[3], ~in_1[2], ~in_1[1], ~in_1[0], I);  // AND_Gate
  and and_2 (and_2_out, ~in_1[7], ~in_1[6], in_1[5], ~in_1[4], ~in_1[3], ~in_1[2], ~in_1[1], ~in_1[0], ~I);  // AND_Gate
  or or_1 (out_3, and_1_out, and_2_out);
endmodule

module s2 (
  input  [7:0] in_1,
  input  I,
  output out_3
);

  wire and_1_out, and_2_out;

  and and_1 (and_1_out, ~in_1[7], in_1[6], ~in_1[5], ~in_1[4], ~in_1[3], ~in_1[2], ~in_1[1], ~in_1[0], I);  // AND_Gate
  and and_2 (and_2_out, ~in_1[7], ~in_1[6], ~in_1[5], in_1[4], ~in_1[3], ~in_1[2], ~in_1[1], ~in_1[0], ~I);  // AND_Gate
  or or_1 (out_3, and_1_out, and_2_out);
endmodule

module s3 (
  input  [7:0] in_1,
  input  I,
  output out_3
);

  wire and_1_out, and_2_out;

  and and_1 (and_1_out, ~in_1[7], ~in_1[6], in_1[5], ~in_1[4], ~in_1[3], ~in_1[2], ~in_1[1], ~in_1[0], I);  // AND_Gate
  and and_2 (and_2_out, ~in_1[7], ~in_1[6], ~in_1[5], ~in_1[4], in_1[3], ~in_1[2], ~in_1[1], ~in_1[0], ~I);  // AND_Gate
  or or_1 (out_3, and_1_out, and_2_out);
endmodule

module s4 (
  input  [7:0] in_1,
  input  I,
  output out_3
);

  wire and_1_out, and_2_out;

  and and_1 (and_1_out, ~in_1[7], ~in_1[6], ~in_1[5], ~in_1[4], ~in_1[3], in_1[2], ~in_1[1], ~in_1[0], ~I);  // AND_Gate
  and and_2 (and_2_out, ~in_1[7], ~in_1[6], ~in_1[5], in_1[4], ~in_1[3], ~in_1[2], ~in_1[1], ~in_1[0], I);  // AND_Gate
  or or_1 (out_3, and_1_out, and_2_out);
endmodule

module s5 (
  input  [7:0] in_1,
  input  I,
  output out_3
);

  wire and_1_out, and_2_out;

  and and_1 (and_1_out, ~in_1[7], ~in_1[6], ~in_1[5], ~in_1[4], ~in_1[3], ~in_1[2], in_1[1], ~in_1[0], ~I);  // AND_Gate
  and and_2 (and_2_out, ~in_1[7], ~in_1[6], ~in_1[5], ~in_1[4], in_1[3], ~in_1[2], ~in_1[1], ~in_1[0], I);  // AND_Gate
  or or_1 (out_3, and_1_out, and_2_out);
endmodule

module s6 (
  input  [7:0] in_1,
  input  I,
  output out_3
);

  wire and_1_out, and_2_out;

  and and_1 (and_1_out, ~in_1[7], ~in_1[6], ~in_1[5], ~in_1[4], ~in_1[3], ~in_1[2], ~in_1[1], in_1[0], ~I);  // AND_Gate
  and and_2 (and_2_out, ~in_1[7], ~in_1[6], ~in_1[5], ~in_1[4], ~in_1[3], in_1[2], ~in_1[1], ~in_1[0], I);  // AND_Gate
  or or_1 (out_3, and_1_out, and_2_out);
endmodule

module s7 (
  input  [7:0] in_1,
  input  I,
  output out_3
);

  wire and_1_out, and_2_out;

  and and_1 (and_1_out, ~in_1[7], ~in_1[6], ~in_1[5], ~in_1[4], ~in_1[3], ~in_1[2], in_1[1], ~in_1[0], I);  // AND_Gate
  and and_2 (and_2_out, ~in_1[7], ~in_1[6], ~in_1[5], ~in_1[4], ~in_1[3], ~in_1[2], ~in_1[1], in_1[0], I);  // AND_Gate
  or or_1 (out_3, and_1_out, and_2_out);
endmodule

module PlayerPos (
  input  LR,
  input  MOVE,
  input  CLOCK,
  output [7:0] out_4
);

  wire and_1_out, or_1_out;
  wire [7:0] s7_1_out_3;

  s0 s0_1 (.in_1(out_4), .out_3(s7_1_out_3[7]), .I(LR));
  s1 s1_1 (.in_1(out_4), .out_3(s7_1_out_3[6]), .I(LR));
  s2 s2_1 (.in_1(out_4), .out_3(s7_1_out_3[5]), .I(LR));
  s3 s3_1 (.in_1(out_4), .out_3(s7_1_out_3[4]), .I(LR));
  s4 s4_1 (.in_1(out_4), .out_3(s7_1_out_3[3]), .I(LR));
  s5 s5_1 (.in_1(out_4), .out_3(s7_1_out_3[2]), .I(LR));
  s6 s6_1 (.in_1(out_4), .out_3(s7_1_out_3[1]), .I(LR));
  s7 s7_1 (.in_1(out_4), .out_3(s7_1_out_3[0]), .I(LR));
  or or_1 (or_1_out, MOVE, and_1_out);
  Register register_1 (.D(s7_1_out_3), .en(or_1_out), .Q(out_4), .clk(CLOCK));  // open: clr
  and and_1 (and_1_out, ~out_4[7], ~out_4[6], ~out_4[5], ~out_4[4], ~out_4[3], ~out_4[2], ~out_4[1], ~out_4[0]);  // AND_Gate
endmodule

module main (
);

  wire and_1_out, and_2_out, clock_1_out, or_1_out;
  wire [3:0] joystick_1_x;
  wire [4:0] ship_1_out_2, ship_1_out_3, ship_1_out_4, ship_1_out_5, ship_1_out_6, ship_2_out_2,
       ship_2_out_3, ship_2_out_4, ship_2_out_5, ship_2_out_6, ship_3_out_2, ship_3_out_3, ship_3_out_4,
       ship_3_out_5, ship_3_out_6, ship_4_out_2, ship_4_out_3, ship_4_out_4, ship_4_out_5, ship_4_out_6,
       ship_5_out_2, ship_5_out_3, ship_5_out_4, ship_5_out_5, ship_5_out_6, ship_6_out_2, ship_6_out_3,
       ship_6_out_4, ship_6_out_5, ship_6_out_6, ship_7_out_2, ship_7_out_3, ship_7_out_4, ship_7_out_5,
       ship_7_out_6, ship_8_out_2, ship_8_out_3, ship_8_out_4, ship_8_out_5, ship_8_out_6;
  wire [7:0] player_1_position;

  DotMatrix #(.matrixrows(5)) dotmatrix_1 (
    .col0(ship_2_out_2), .col1(ship_2_out_3), .col2(ship_2_out_4), .col3(ship_2_out_5), .col4(ship_2_out_6));
  DotMatrix #(.matrixrows(5)) dotmatrix_2 (
    .col0(ship_1_out_2), .col1(ship_1_out_3), .col2(ship_1_out_4), .col3(ship_1_out_5), .col4(ship_1_out_6));
  ship ship_1 (
    .out_2(ship_1_out_2), .out_3(ship_1_out_3), .out_4(ship_1_out_4), .out_5(ship_1_out_5),
    .out_6(ship_1_out_6), .in_1(player_1_position[7]));
  Clock clock_1 (.out(clock_1_out));
  DotMatrix #(.matrixrows(5)) dotmatrix_3 (
    .col0(ship_4_out_2), .col1(ship_4_out_3), .col2(ship_4_out_4), .col3(ship_4_out_5), .col4(ship_4_out_6));
  ship ship_2 (
    .out_2(ship_2_out_2), .out_3(ship_2_out_3), .out_4(ship_2_out_4), .out_5(ship_2_out_5),
    .out_6(ship_2_out_6), .in_1(player_1_position[6]));
  or or_1 (or_1_out, joystick_1_x[0], joystick_1_x[1], joystick_1_x[2]);
  DotMatrix #(.matrixrows(5)) dotmatrix_4 (
    .col0(ship_6_out_2), .col1(ship_6_out_3), .col2(ship_6_out_4), .col3(ship_6_out_5), .col4(ship_6_out_6));
  ship ship_3 (
    .out_2(ship_3_out_2), .out_3(ship_3_out_3), .out_4(ship_3_out_4), .out_5(ship_3_out_5),
    .out_6(ship_3_out_6), .in_1(player_1_position[4]));
  DotMatrix #(.matrixrows(5)) dotmatrix_5 (
    .col0(ship_3_out_2), .col1(ship_3_out_3), .col2(ship_3_out_4), .col3(ship_3_out_5), .col4(ship_3_out_6));
  ship ship_4 (
    .out_2(ship_4_out_2), .out_3(ship_4_out_3), .out_4(ship_4_out_4), .out_5(ship_4_out_5),
    .out_6(ship_4_out_6), .in_1(player_1_position[5]));
  player player_1 (.L_button(and_1_out), .R_button(and_2_out), .Clock(clock_1_out), .position(player_1_position));
  and and_1 (and_1_out, or_1_out, ~joystick_1_x[3]);  // AND_Gate
  Joystick joystick_1 (.x(joystick_1_x));  // open: y
  ship ship_5 (
    .out_2(ship_5_out_2), .out_3(ship_5_out_3), .out_4(ship_5_out_4), .out_5(ship_5_out_5),
    .out_6(ship_5_out_6), .in_1(player_1_position[2]));
  ship ship_6 (
    .out_2(ship_6_out_2), .out_3(ship_6_out_3), .out_4(ship_6_out_4), .out_5(ship_6_out_5),
    .out_6(ship_6_out_6), .in_1(player_1_position[3]));
  DotMatrix #(.matrixrows(5)) dotmatrix_6 (
    .col0(ship_5_out_2), .col1(ship_5_out_3), .col2(ship_5_out_4), .col3(ship_5_out_5), .col4(ship_5_out_6));
  and and_2 (and_2_out, or_1_out, joystick_1_x[3]);
  DotMatrix #(.matrixrows(5)) dotmatrix_7 (
    .col0(ship_7_out_2), .col1(ship_7_out_3), .col2(ship_7_out_4), .col3(ship_7_out_5), .col4(ship_7_out_6));
  ship ship_7 (
    .out_2(ship_7_out_2), .out_3(ship_7_out_3), .out_4(ship_7_out_4), .out_5(ship_7_out_5),
    .out_6(ship_7_out_6), .in_1(player_1_position[1]));
  DotMatrix #(.matrixrows(5)) dotmatrix_8 (
    .col0(ship_8_out_2), .col1(ship_8_out_3), .col2(ship_8_out_4), .col3(ship_8_out_5), .col4(ship_8_out_6));
  ship ship_8 (
    .out_2(ship_8_out_2), .out_3(ship_8_out_3), .out_4(ship_8_out_4), .out_5(ship_8_out_5),
    .out_6(ship_8_out_6), .in_1(player_1_position[0]));
endmodule

module ship (
  input  in_1,
  output [4:0] out_2,
  output [4:0] out_3,
  output [4:0] out_4,
  output [4:0] out_5,
  output [4:0] out_6
);

  Multiplexer #(.width(5), .enable("false")) multiplexer_1 (.in0({5{1'b0}}), .in1(5'b00001), .out(out_2), .sel(in_1));
  Multiplexer #(.width(5), .enable("false")) multiplexer_2 (.in0({5{1'b0}}), .in1(5'b00011), .out(out_3), .sel(in_1));
  Multiplexer #(.width(5), .enable("false")) multiplexer_3 (.in0({5{1'b0}}), .in1(5'b01111), .out(out_4), .sel(in_1));
  Multiplexer #(.width(5), .enable("false")) multiplexer_4 (.in0({5{1'b0}}), .in1(5'b00011), .out(out_5), .sel(in_1));
  Multiplexer #(.width(5), .enable("false")) multiplexer_5 (.in0({5{1'b0}}), .in1(5'b00001), .out(out_6), .sel(in_1));
endmodule
