// Logisim project talpa.circ as structural Verilog: 2 circuits, main circuit talpa
module talpa (
  input  in_1,
  input  in_2,
  input  Ck,
  output out_4,
  output out_5,
  output [7:0] score
);

  wire and_2_out, and_3_out, and_4_out, and_5_out, and_6_out, demultiplexer_1_out0, demultiplexer_1_out7,
       not_1_out, NT, or_3_out, or_4_out, S, TO;
  wire [2:0] counter_1_q, random_1_out;

  not not_1 (not_1_out, NT);
  and and_1 (NT, ~out_4, ~out_5);  // AND_Gate
  Counter #(.width(3), .max('h7)) counter_1 (
    .count(not_1_out), .Q(counter_1_q), .clk(Ck), .clr(S));  // open: load, D, carry
  and and_2 (and_2_out, in_1, out_4);
  and and_3 (and_3_out, in_2, out_5);
  Random #(.width(3)) random_1 (.clk(Ck), .out(random_1_out));  // open: next, clr
  Demultiplexer #(.select(3), .enable("false")) demultiplexer_1 (
    .out0(demultiplexer_1_out0), .out7(demultiplexer_1_out7), .in(1'b1), .sel(random_1_out));  // open: out1, out2, out3, out4, out5, out6
  and and_4 (and_4_out, counter_1_q[0], counter_1_q[1], counter_1_q[2]);
  or or_1 (TO, and_4_out, S);
  Counter counter_2 (.count(S), .Q(score), .clk(Ck));  // open: load, D, carry, clr
  or or_2 (S, and_2_out, and_3_out);
  and and_5 (and_5_out, demultiplexer_1_out0, NT);
  and and_6 (and_6_out, demultiplexer_1_out7, NT);
  or or_3 (or_3_out, and_5_out, TO);
  or or_4 (or_4_out, and_6_out, TO);
  D_Flip_Flop d_ff_1 (.clk(Ck), .D(and_5_out), .Q(out_4), .en(or_3_out));  // open: Qn, preset, reset
  D_Flip_Flop d_ff_2 (.clk(Ck), .D(and_6_out), .Q(out_5), .en(or_4_out));  // open: Qn, preset, reset

  // Other names for the same wires on the sheet: _1 = in_1; _2 = in_2; C = Ck; T1 = out_4; T2 = out_5
endmodule

module main (
);

  wire _1, _2, clock_1_out, T1, T2;
  wire [7:0] S;

  LED led_1 (.in(T1));
  Button button_1 (.out(_1));
  Clock clock_1 (.out(clock_1_out));
  talpa talpa_1 (.Ck(clock_1_out), .in_1(_1), .in_2(_2), .out_4(T1), .out_5(T2), .score(S));
  LED led_2 (.in(T2));
  Hex_Digit_Display hex_digit_display_1 (.value(S[7:4]));  // open: dp
  Button button_2 (.out(_2));
  Hex_Digit_Display hex_digit_display_2 (.value(S[3:0]));  // open: dp

  // Other names for the same wires on the sheet: S1[3:0] = S[3:0]; S2[3:0] = S[7:4]
endmodule
