// Logisim project Progetto.circ as structural Verilog: 9 circuits, main circuit Spegni le luci
module Spegni_le_luci (
);

  wire clock_1_out, controllo_input_1_out_0, controllo_input_1_out_1, controllo_input_1_out_2,
       controllo_input_1_out_3, controllo_input_1_out_4, controllo_input_1_out_5, controllo_input_1_out_6,
       controllo_input_1_out_7, controllo_input_1_out_8, Err, In_1, In_2, In_3, In_4, In_5, In_6, In_7, In_8,
       In_9, inizio_casuale_1_out_2, inizio_casuale_1_out_3, inizio_casuale_1_out_4, inizio_casuale_1_out_5,
       inizio_casuale_1_out_6, inizio_casuale_1_out_7, inizio_casuale_1_out_9, inizio_casuale_1_out_10,
       inizio_casuale_1_out_11, modifica_input_1_out_1, modifica_input_1_out_2, modifica_input_1_out_3,
       modifica_input_1_out_4, modifica_input_1_out_5, modifica_input_1_out_6, modifica_input_1_out_7,
       modifica_input_1_out_8, modifica_input_1_out_9, Off, On___off, or_1_out, Out_1, Out_2, Out_3, Out_4,
       Out_5, Out_6, Out_7, Out_8, Out_9, Reset, selezione_input_1_out_19, selezione_input_1_out_20,
       selezione_input_1_out_21, selezione_input_1_out_22, selezione_input_1_out_23,
       selezione_input_1_out_24, selezione_input_1_out_25, selezione_input_1_out_26,
       selezione_input_1_out_27, Vittoria;
  wire [3:0] k, k_prime, k_t, T1, T2, T3, T4;

  Button button_1 (.out(In_2));
  Button button_2 (.out(In_1));
  Button button_3 (.out(In_4));
  Button button_4 (.out(In_5));
  Button button_5 (.out(In_8));
  Button button_6 (.out(In_7));
  Button button_7 (.out(On___off));
  LED led_1 (.in(Err));
  Hex_Digit_Display hex_digit_display_1 (.value(T2));  // open: dp
  Hex_Digit_Display hex_digit_display_2 (.value(T1));  // open: dp
  Button button_8 (.out(In_3));
  Button button_9 (.out(In_6));
  Button button_10 (.out(In_9));
  Button button_11 (.out(Reset));
  Controllo_input controllo_input_1 (
    .In_0(In_1), .In_1(In_2), .In_2(In_3), .In_3(In_4), .In_4(In_5), .In_5(In_6), .In_6(In_7), .In_7(In_8),
    .In_8(In_9), .On___off(On___off), .Off(Off), .Vittoria(Vittoria), .Out_0(controllo_input_1_out_0),
    .Out_1(controllo_input_1_out_1), .Out_2(controllo_input_1_out_2), .Out_3(controllo_input_1_out_3),
    .Out_4(controllo_input_1_out_4), .Out_5(controllo_input_1_out_5), .Out_6(controllo_input_1_out_6),
    .Out_7(controllo_input_1_out_7), .Out_8(controllo_input_1_out_8));
  Modifica_input modifica_input_1 (
    .In_1(controllo_input_1_out_0), .In_2(controllo_input_1_out_1), .In_3(controllo_input_1_out_2),
    .In_4(controllo_input_1_out_3), .In_5(controllo_input_1_out_4), .In_6(controllo_input_1_out_5),
    .In_7(controllo_input_1_out_6), .In_8(controllo_input_1_out_7), .In_9(controllo_input_1_out_8),
    .Out_1(modifica_input_1_out_1), .Out_2(modifica_input_1_out_2), .Out_3(modifica_input_1_out_3),
    .Out_4(modifica_input_1_out_4), .Out_5(modifica_input_1_out_5), .Out_6(modifica_input_1_out_6),
    .Out_7(modifica_input_1_out_7), .Out_8(modifica_input_1_out_8), .Out_9(modifica_input_1_out_9));
  Inizio_casuale inizio_casuale_1 (
    .On___off(or_1_out), .Errore(Err), .out_2(inizio_casuale_1_out_2), .out_5(inizio_casuale_1_out_5),
    .out_11(inizio_casuale_1_out_11), .out_3(inizio_casuale_1_out_3), .out_9(inizio_casuale_1_out_9),
    .out_10(inizio_casuale_1_out_10), .out_6(inizio_casuale_1_out_6), .out_4(inizio_casuale_1_out_4),
    .out_7(inizio_casuale_1_out_7));
  or or_1 (or_1_out, On___off, Reset);
  Hex_Digit_Display hex_digit_display_3 (.value(T4));  // open: dp
  Hex_Digit_Display hex_digit_display_4 (.value(T3));  // open: dp
  Contatore contatore_1 (
    .k_prime(k_prime), .k(k), .Off(Off), .Reset(Reset), .In_1(In_1), .In_2(In_2), .In_3(In_3), .In_4(In_4),
    .In_5(In_5), .In_6(In_6), .In_7(In_7), .In_8(In_8), .In_9(In_9), .Vittoria(Vittoria), .k_2(k_t));
  LED led_2 (.in(Vittoria));
  Display display_1 (
    .I0(selezione_input_1_out_19), .I1(selezione_input_1_out_20), .I2(selezione_input_1_out_21),
    .I3(selezione_input_1_out_22), .I4(selezione_input_1_out_23), .I5(selezione_input_1_out_24),
    .I6(selezione_input_1_out_25), .I7(selezione_input_1_out_26), .I8(selezione_input_1_out_27), .Q0(Out_1),
    .Q1(Out_2), .Q2(Out_3), .Q3(Out_4), .Q4(Out_5), .Q5(Out_6), .Q6(Out_7), .Q7(Out_8), .Q8(Out_9), .Off(Off));
  Selezione_input selezione_input_1 (
    .in_1(modifica_input_1_out_1), .in_2(modifica_input_1_out_2), .in_3(modifica_input_1_out_3),
    .in_4(modifica_input_1_out_4), .in_5(modifica_input_1_out_5), .in_6(modifica_input_1_out_6),
    .in_7(modifica_input_1_out_7), .in_8(modifica_input_1_out_8), .in_9(modifica_input_1_out_9),
    .in_10(inizio_casuale_1_out_2), .in_11(inizio_casuale_1_out_5), .in_12(inizio_casuale_1_out_11),
    .in_13(inizio_casuale_1_out_3), .in_14(inizio_casuale_1_out_9), .in_15(inizio_casuale_1_out_10),
    .in_16(inizio_casuale_1_out_6), .in_17(inizio_casuale_1_out_4), .in_18(inizio_casuale_1_out_7),
    .out_19(selezione_input_1_out_19), .out_20(selezione_input_1_out_20), .out_21(selezione_input_1_out_21),
    .out_22(selezione_input_1_out_22), .out_23(selezione_input_1_out_23), .out_24(selezione_input_1_out_24),
    .out_25(selezione_input_1_out_25), .out_26(selezione_input_1_out_26), .out_27(selezione_input_1_out_27));
  Hex_Digit_Display hex_digit_display_5 (.value(k_t));  // open: dp
  Hex_Digit_Display hex_digit_display_6 (.value(k));  // open: dp
  Hex_Digit_Display hex_digit_display_7 (.value(k_prime));  // open: dp
  LED led_3 (.in(Out_1));
  LED led_4 (.in(Out_4));
  LED led_5 (.in(Out_7));
  Vittoria vittoria_1 (
    .Out_1(Out_1), .Out_2(Out_2), .Out_3(Out_3), .Out_4(Out_4), .Out_5(Out_5), .Out_6(Out_6), .Out_7(Out_7),
    .Out_8(Out_8), .Out_9(Out_9), .Off(Off), .Vittoria(Vittoria), .Err(Err));
  Clock clock_1 (.out(clock_1_out));
  Cronometro cronometro_1 (
    .T1(T1), .T2(T2), .T3(T3), .T4(T4), .in_1(On___off), .Off(Off), .Reset(Reset), .Clock(clock_1_out),
    .Vittoria(Vittoria));
  LED led_6 (.in(Out_2));
  LED led_7 (.in(Out_5));
  LED led_8 (.in(Out_8));
  LED led_9 (.in(Out_3));
  LED led_10 (.in(Out_6));
  LED led_11 (.in(Out_9));

  // Notes on the sheet:
  //   Minuti
  //   In caso di errore, premere il tasto Reset
  //   Secondi
  //   Contatore & cronometro
  //   Numero mosse
  //   Circuito principale
endmodule

// Mosse
module Contatore (
  input  Off,
  input  Reset,
  input  Vittoria,
  input  In_1,
  input  In_2,
  input  In_3,
  input  In_4,
  input  In_5,
  input  In_6,
  input  In_7,
  input  In_8,
  input  In_9,
  output [3:0] k_prime,
  output [3:0] k,
  output [3:0] k_2
);

  wire and_1_out, and_2_out, and_3_out, and_4_out, and_5_out, and_6_out, and_7_out, and_8_out, and_9_out,
       and_10_out, i, or_1_out, t_prime, t_prime_prime;

  Counter #(.width(4), .max('h9)) counter_1 (
    .count(i), .Q(k_prime), .carry(t_prime), .clk(i), .clr(or_1_out));  // open: load, D
  Counter #(.width(4), .max('h9)) counter_2 (
    .count(t_prime), .Q(k), .carry(t_prime_prime), .clk(i), .clr(or_1_out));  // open: load, D
  or or_1 (or_1_out, Off, Reset);
  and and_1 (and_1_out, t_prime_prime, t_prime);
  and and_2 (and_2_out, In_1, ~Vittoria);  // AND_Gate
  Counter #(.width(4), .max('h9)) counter_3 (
    .count(and_1_out), .Q(k_2), .clk(i), .clr(or_1_out));  // open: load, D, carry
  and and_3 (and_3_out, In_3, ~Vittoria);  // AND_Gate
  and and_4 (and_4_out, In_2, ~Vittoria);  // AND_Gate
  or or_2 (i, and_2_out, and_4_out, and_3_out, and_5_out, and_6_out, and_7_out, and_8_out, and_9_out, and_10_out);
  and and_5 (and_5_out, In_4, ~Vittoria);  // AND_Gate
  and and_6 (and_6_out, In_5, ~Vittoria);  // AND_Gate
  and and_7 (and_7_out, In_6, ~Vittoria);  // AND_Gate
  and and_8 (and_8_out, In_7, ~Vittoria);  // AND_Gate
  and and_9 (and_9_out, In_8, ~Vittoria);  // AND_Gate
  and and_10 (and_10_out, In_9, ~Vittoria);  // AND_Gate
endmodule

// On / off
module Controllo_input (
  input  Vittoria,
  input  In_0,
  input  In_1,
  input  In_2,
  input  In_3,
  input  In_4,
  input  In_5,
  input  In_6,
  input  In_7,
  input  In_8,
  input  On___off,
  output Out_0,
  output Out_1,
  output Out_2,
  output Out_3,
  output Out_4,
  output Out_5,
  output Out_6,
  output Out_7,
  output Out_8,
  output Off
);

  wire and_1_out, and_2_out, and_3_out, and_4_out, and_5_out, and_6_out, and_7_out, and_8_out, and_9_out,
       t_ff_1_q;

  and and_1 (and_1_out, t_ff_1_q, In_0);
  and and_2 (and_2_out, t_ff_1_q, In_1);
  and and_3 (and_3_out, t_ff_1_q, In_2);
  and and_4 (and_4_out, t_ff_1_q, In_3);
  and and_5 (and_5_out, t_ff_1_q, In_4);
  and and_6 (and_6_out, t_ff_1_q, In_5);
  and and_7 (and_7_out, t_ff_1_q, In_6);
  and and_8 (and_8_out, t_ff_1_q, In_7);
  and and_9 (and_9_out, t_ff_1_q, In_8);
  T_Flip_Flop t_ff_1 (.clk(On___off), .T(On___off), .Q(t_ff_1_q), .Qn(Off));  // open: preset, reset, en
  and and_10 (Out_0, ~Vittoria, and_1_out);  // AND_Gate
  and and_11 (Out_1, ~Vittoria, and_2_out);  // AND_Gate
  and and_12 (Out_2, ~Vittoria, and_3_out);  // AND_Gate
  and and_13 (Out_3, ~Vittoria, and_4_out);  // AND_Gate
  and and_14 (Out_4, ~Vittoria, and_5_out);  // AND_Gate
  and and_15 (Out_5, ~Vittoria, and_6_out);  // AND_Gate
  and and_16 (Out_6, ~Vittoria, and_7_out);  // AND_Gate
  and and_17 (Out_7, ~Vittoria, and_8_out);  // AND_Gate
  and and_18 (Out_8, ~Vittoria, and_9_out);  // AND_Gate
endmodule

// Tempo
module Cronometro (
  input  in_1,
  input  Clock,
  input  Vittoria,
  input  Reset,
  input  Off,
  output [3:0] T1,
  output [3:0] T2,
  output [3:0] T3,
  output [3:0] T4
);

  wire and_1_out, counter_2_carry, counter_3_carry, counter_4_carry, d_ff_1_q, or_1_out;

  D_Flip_Flop d_ff_1 (.clk(in_1), .D(in_1), .Q(d_ff_1_q));  // open: Qn, preset, en, reset
  Counter #(.width(4), .max('h5), .trigger("falling")) counter_1 (
    .count(d_ff_1_q), .Q(T1), .clk(counter_2_carry), .clr(or_1_out));  // open: load, D, carry
  Counter #(.width(4), .max('h9), .trigger("falling")) counter_2 (
    .count(d_ff_1_q), .Q(T2), .carry(counter_2_carry), .clk(counter_3_carry), .clr(or_1_out));  // open: load, D
  Counter #(.width(4), .max('h5), .trigger("falling")) counter_3 (
    .count(d_ff_1_q), .Q(T3), .carry(counter_3_carry), .clk(counter_4_carry), .clr(or_1_out));  // open: load, D
  and and_1 (and_1_out, Clock, ~Vittoria);  // AND_Gate
  or or_1 (or_1_out, Reset, Off);
  Counter #(.width(4), .max('h9), .trigger("falling")) counter_4 (
    .count(d_ff_1_q), .Q(T4), .carry(counter_4_carry), .clk(and_1_out), .clr(or_1_out));  // open: load, D
endmodule

// Output
module Display (
  input  I0,
  input  I1,
  input  I2,
  input  I3,
  input  I4,
  input  I5,
  input  Off,
  input  I6,
  input  I7,
  input  I8,
  output Q0,
  output Q1,
  output Q2,
  output Q3,
  output Q4,
  output Q5,
  output Q6,
  output Q7,
  output Q8
);

  T_Flip_Flop t_ff_1 (.clk(I0), .T(I0), .Q(Q0), .reset(Off));  // open: Qn, preset, en
  T_Flip_Flop t_ff_2 (.clk(I3), .T(I3), .Q(Q3), .reset(Off));  // open: Qn, preset, en
  T_Flip_Flop t_ff_3 (.clk(I6), .T(I6), .Q(Q6), .reset(Off));  // open: Qn, preset, en
  T_Flip_Flop t_ff_4 (.clk(I1), .T(I1), .Q(Q1), .reset(Off));  // open: Qn, preset, en
  T_Flip_Flop t_ff_5 (.clk(I4), .T(I4), .Q(Q4), .reset(Off));  // open: Qn, preset, en
  T_Flip_Flop t_ff_6 (.clk(I7), .T(I7), .Q(Q7), .reset(Off));  // open: Qn, preset, en
  T_Flip_Flop t_ff_7 (.clk(I2), .T(I2), .Q(Q2), .reset(Off));  // open: Qn, preset, en
  T_Flip_Flop t_ff_8 (.clk(I5), .T(I5), .Q(Q5), .reset(Off));  // open: Qn, preset, en
  T_Flip_Flop t_ff_9 (.clk(I8), .T(I8), .Q(Q8), .reset(Off));  // open: Qn, preset, en

  // Notes on the sheet:
  //   Per memorizzare quali luci sono accese o spente
endmodule

// Start
module Inizio_casuale (
  input  On___off,
  output out_2,
  output out_3,
  output out_4,
  output out_5,
  output out_6,
  output out_7,
  output Errore,
  output out_9,
  output out_10,
  output out_11
);

  wire or_1_out, or_2_out, or_3_out, R0, R1, R2, R3, R4, R5, R6, R7, R8, random_2_out, random_3_out,
       random_4_out, random_5_out, random_6_out, random_7_out, random_8_out, random_9_out, random_10_out;

  Random #(.width(9)) random_1 (.clk(On___off), .out({R8, R7, R6, R5, R4, R3, R2, R1, R0}));  // open: next, clr
  Random #(.width(1), .seed(1)) random_2 (.clk(R0), .out(random_2_out));  // open: next, clr
  Random #(.width(1), .seed(4)) random_3 (.clk(R3), .out(random_3_out));  // open: next, clr
  Random #(.width(1), .seed(7)) random_4 (.clk(R6), .out(random_4_out));  // open: next, clr
  and and_1 (out_2, On___off, random_2_out);
  and and_2 (out_5, On___off, random_3_out);
  and and_3 (out_9, On___off, random_4_out);
  Random #(.width(1), .seed(2)) random_5 (.clk(R1), .out(random_5_out));  // open: next, clr
  Random #(.width(1), .seed(5)) random_6 (.clk(R4), .out(random_6_out));  // open: next, clr
  Random #(.width(1), .seed(8)) random_7 (.clk(R7), .out(random_7_out));  // open: next, clr
  and and_4 (out_3, On___off, random_5_out);
  and and_5 (out_6, On___off, random_6_out);
  and and_6 (out_10, On___off, random_7_out);
  Random #(.width(1), .seed(3)) random_8 (.clk(R2), .out(random_8_out));  // open: next, clr
  Random #(.width(1), .seed(6)) random_9 (.clk(R5), .out(random_9_out));  // open: next, clr
  Random #(.width(1), .seed(9)) random_10 (.clk(R8), .out(random_10_out));  // open: next, clr
  and and_7 (out_4, On___off, random_8_out);
  and and_8 (out_7, On___off, random_9_out);
  and and_9 (out_11, On___off, random_10_out);
  or or_1 (or_1_out, random_8_out, random_5_out, random_2_out);
  or or_2 (or_2_out, random_9_out, random_6_out, random_3_out);
  or or_3 (or_3_out, random_10_out, random_7_out, random_4_out);
  nor nor_1 (Errore, or_1_out, or_2_out, or_3_out);

  // Other names for the same wires on the sheet: In = On___off
endmodule

// Propagazione
module Modifica_input (
  input  In_1,
  input  In_2,
  input  In_3,
  input  In_4,
  input  In_5,
  input  In_6,
  input  In_7,
  input  In_8,
  input  In_9,
  output Out_1,
  output Out_2,
  output Out_3,
  output Out_4,
  output Out_5,
  output Out_6,
  output Out_7,
  output Out_8,
  output Out_9
);

  or or_1 (Out_1, In_1, In_2, In_4);
  or or_2 (Out_2, In_2, In_1, In_3, In_5);
  or or_3 (Out_3, In_3, In_2, In_6);
  or or_4 (Out_4, In_4, In_1, In_5, In_7);
  or or_5 (Out_5, In_5, In_2, In_4, In_6, In_8);
  or or_6 (Out_6, In_6, In_3, In_5, In_9);
  or or_7 (Out_7, In_7, In_4, In_8);
  or or_8 (Out_8, In_8, In_5, In_7, In_9);
  or or_9 (Out_9, In_9, In_6, In_8);
endmodule

// Selezione
module Selezione_input (
  input  in_1,
  input  in_2,
  input  in_3,
  input  in_4,
  input  in_5,
  input  in_6,
  input  in_7,
  input  in_8,
  input  in_9,
  input  in_10,
  input  in_11,
  input  in_12,
  input  in_13,
  input  in_14,
  input  in_15,
  input  in_16,
  input  in_17,
  input  in_18,
  output out_19,
  output out_20,
  output out_21,
  output out_22,
  output out_23,
  output out_24,
  output out_25,
  output out_26,
  output out_27
);

  or or_1 (out_19, in_1, in_10);
  or or_2 (out_20, in_2, in_11);
  or or_3 (out_21, in_3, in_12);
  or or_4 (out_22, in_4, in_13);
  or or_5 (out_23, in_5, in_14);
  or or_6 (out_24, in_6, in_15);
  or or_7 (out_25, in_7, in_16);
  or or_8 (out_26, in_8, in_17);
  or or_9 (out_27, in_9, in_18);

  // Other names for the same wires on the sheet: In_0 = in_1; In_1_t = in_2; In_2_t = in_3; In_3_t = in_4;
  //   In_4_t = in_5; In_5_t = in_6; In_6_t = in_7; In_7_t = in_8; In_8_t = in_9; R0 = in_10; R1 = in_11; R2 = in_12;
  //   R3 = in_13; R4 = in_14; R5 = in_15; R6 = in_16; R7 = in_17; R8 = in_18
endmodule

// Game Over
module Vittoria (
  input  Out_1,
  input  Out_2,
  input  Out_3,
  input  Out_4,
  input  Out_5,
  input  Out_6,
  input  Out_7,
  input  Out_8,
  input  Out_9,
  input  Off,
  input  Err,
  output Vittoria
);

  wire and_1_out, nor_1_out;

  nor nor_1 (nor_1_out, Out_1, Out_2, Out_3, Out_4, Out_5, Out_6, Out_7, Out_8, Out_9);
  and and_1 (and_1_out, nor_1_out, ~Off);  // AND_Gate
  and and_2 (Vittoria, and_1_out, ~Err);  // AND_Gate
endmodule
